# Fritzing sketch Wiring (saved by Fritzing 0.9.3b)
circuit board: 5.45948cm x 1.94147cm
breadboards: 1

parts:
  Raspberry_Pi_1 = Raspberry Pi 3 [part_number=RPI-3-V1.2]
  YL-1 = YL-38 Humitidy Sensor
  IC1 = MCP3008 8-channel 10-bit ADC [part_number=MCP3008]
  DHT1 = DHT22 Humidity and Temperature Sensor
  R1 = Resistor [tolerance=±5% resistance=10k package=THT]
  LED1 = LED - 5mm [color="Red (633nm)" package="5 mm [THT]"]
  R2 = Resistor [tolerance=±5% resistance=100 package=THT]

nets:
  3V3: Raspberry_Pi_1.3v3, Raspberry_Pi_1.3V3, YL-1.VCC, DHT1.VDD, R1.Pin_0
  N1: Raspberry_Pi_1.GPIO2, DHT1.DATA, R1.Pin_1
  GND: Raspberry_Pi_1.GND, YL-1.GND, DHT1.GND, LED1.cathode
  N2: Raspberry_Pi_1.GPIO25, LED1.anode, R2.Pin_0, R2.Pin_1
  N3: YL-1.ANALOG, IC1.no_name_yet#1
  N4: IC1.no_name_yet#6, IC1.no_name_yet#7, IC1.no_name_yet#10, IC1.no_name_yet#11, IC1.no_name_yet#14
